// Logisim project control-logic.circ as structural Verilog: 1 circuit, main circuit control_logic
module control_logic (
  input  [31:0] inst,
  input  BrEq,
  input  BrLt,
  output PCSel,
  output RegWEn,
  output [2:0] ImmSel,
  output BrUn,
  output ASel,
  output BSel,
  output [3:0] ALUSel,
  output MemRW,
  output [1:0] WBSel,
  output CSRSel,
  output CSRWen
);

  wire alu, and_8_out, and_27_out, and_28_out, and_29_out, and_30_out, and_31_out, and_32_out, and_33_out,
       auipc, BrGe, comparator_1_eq, comparator_2_eq, comparator_3_eq, comparator_4_eq, comparator_5_eq,
       comparator_6_eq, comparator_7_eq, comparator_8_eq, comparator_9_eq, comparator_10_eq,
       comparator_11_eq, comparator_12_eq, comparator_22_eq, comparator_23_eq, comparator_24_eq,
       comparator_25_eq, comparator_26_eq, comparator_27_eq, comparator_28_eq, comparator_29_eq,
       comparator_30_eq, comparator_31_eq, comparator_32_eq, comparator_33_eq, comparator_34_eq,
       comparator_35_eq, comparator_37_eq, comparator_38_eq, comparator_39_eq, comparator_40_eq,
       comparator_41_eq, comparator_42_eq, I, I0, I1, I2, I3, Iaddi, Iandi, Icsrw, Icsrwi, Ilb, Ilh, ILoad,
       Ilw, Iori, Islli, Islti, Israi, Isrli, Ixori, jal, lui, not_1_out, not_4_out, not_5_out, not_6_out,
       or_4_out, or_6_out, or_9_out, or_11_out, R, R_or, Radd, Rand, Rmul, Rmulh, Rmulhu, Rsll, Rslt, Rsra,
       Rsrl, Rsub, Rxor, SB, SBbeq, SBbge, SBbgeu, SBblt, SBbltu, SBbne, U, U0, U1;
  wire [3:0] ALUSel_I, ALUSel_R, priority_encoder_3_out, priority_encoder_4_out;

  or or_1 (I, I0, I1, I2, I3);
  Comparator #(.width(3)) comparator_1 (.a(inst[14:12]), .b(3'b000), .eq(comparator_1_eq));  // open: gt, lt
  Comparator #(.width(3)) comparator_2 (.a(inst[14:12]), .b(3'b001), .eq(comparator_2_eq));  // open: gt, lt
  Comparator #(.width(3)) comparator_3 (.a(inst[14:12]), .b(3'b010), .eq(comparator_3_eq));  // open: gt, lt
  Comparator #(.width(3)) comparator_4 (.a(inst[14:12]), .b(3'b000), .eq(comparator_4_eq));  // open: gt, lt
  Comparator #(.width(3)) comparator_5 (.a(inst[14:12]), .b(3'b001), .eq(comparator_5_eq));  // open: gt, lt
  Comparator #(.width(3)) comparator_6 (.a(inst[14:12]), .b(3'b010), .eq(comparator_6_eq));  // open: gt, lt
  Comparator #(.width(3)) comparator_7 (.a(inst[14:12]), .b(3'b100), .eq(comparator_7_eq));  // open: gt, lt
  Comparator #(.width(3)) comparator_8 (.a(inst[14:12]), .b(3'b101), .eq(comparator_8_eq));  // open: gt, lt
  Comparator #(.width(3)) comparator_9 (.a(inst[14:12]), .b(3'b110), .eq(comparator_9_eq));  // open: gt, lt
  Comparator #(.width(3)) comparator_10 (.a(inst[14:12]), .b(3'b111), .eq(comparator_10_eq));  // open: gt, lt
  Comparator #(.width(3)) comparator_11 (.a(inst[14:12]), .b(3'b001), .eq(comparator_11_eq));  // open: gt, lt
  Comparator #(.width(3)) comparator_12 (.a(inst[14:12]), .b(3'b101), .eq(comparator_12_eq));  // open: gt, lt
  or or_2 (U, U1, U0);
  Comparator #(.width(7)) comparator_13 (.a(inst[6:0]), .b(7'b1101111), .eq(jal));  // open: gt, lt
  Comparator #(.width(7)) comparator_14 (.a(inst[6:0]), .b(7'b0110111), .eq(U1));  // open: gt, lt
  Comparator #(.width(7)) comparator_15 (.a(inst[6:0]), .b(7'b0010111), .eq(U0));  // open: gt, lt
  Comparator #(.width(7)) comparator_16 (.a(inst[6:0]), .b(7'b1100011), .eq(SB));  // open: gt, lt
  Comparator #(.width(7)) comparator_17 (.a(inst[6:0]), .b(7'b0100011), .eq(MemRW));  // open: gt, lt
  Comparator #(.width(7)) comparator_18 (.a(inst[6:0]), .b(7'b0000011), .eq(I0));  // open: gt, lt
  Comparator #(.width(7)) comparator_19 (.a(inst[6:0]), .b(7'b1100111), .eq(I2));  // open: gt, lt
  Comparator #(.width(7)) comparator_20 (.a(inst[6:0]), .b(7'b1110011), .eq(I3));  // open: gt, lt
  and and_1 (Ilb, I0, comparator_1_eq);
  and and_2 (Ilh, I0, comparator_2_eq);
  and and_3 (Ilw, I0, comparator_3_eq);
  and and_4 (Iaddi, I1, comparator_4_eq);
  and and_5 (Islli, I1, comparator_5_eq);
  and and_6 (Islti, I1, comparator_6_eq);
  and and_7 (Ixori, I1, comparator_7_eq);
  and and_8 (and_8_out, I1, comparator_8_eq);
  and and_9 (Iori, I1, comparator_9_eq);
  and and_10 (Iandi, I1, comparator_10_eq);
  and and_11 (Icsrw, I3, comparator_11_eq);
  and and_12 (Icsrwi, I3, comparator_12_eq);
  or or_3 (ILoad, Ilw, Ilh, Ilb);
  Comparator #(.width(7)) comparator_21 (.a(inst[6:0]), .b(7'b0110011), .eq(R));  // open: gt, lt
  Comparator #(.width(3)) comparator_22 (.a(inst[14:12]), .b(3'b000), .eq(comparator_22_eq));  // open: gt, lt
  Comparator #(.width(7)) comparator_23 (.a(inst[31:25]), .b({7{1'b0}}), .eq(comparator_23_eq));  // open: gt, lt
  Comparator #(.width(7)) comparator_24 (.a(inst[31:25]), .b(7'b0000001), .eq(comparator_24_eq));  // open: gt, lt
  Comparator #(.width(7)) comparator_25 (.a(inst[31:25]), .b(7'b0100000), .eq(comparator_25_eq));  // open: gt, lt
  Comparator #(.width(3)) comparator_26 (.a(inst[14:12]), .b(3'b001), .eq(comparator_26_eq));  // open: gt, lt
  Comparator #(.width(3)) comparator_27 (.a(inst[14:12]), .b(3'b011), .eq(comparator_27_eq));  // open: gt, lt
  Comparator #(.width(3)) comparator_28 (.a(inst[14:12]), .b(3'b010), .eq(comparator_28_eq));  // open: gt, lt
  Comparator #(.width(3)) comparator_29 (.a(inst[14:12]), .b(3'b100), .eq(comparator_29_eq));  // open: gt, lt
  Comparator #(.width(3)) comparator_30 (.a(inst[14:12]), .b(3'b101), .eq(comparator_30_eq));  // open: gt, lt
  Comparator #(.width(3)) comparator_31 (.a(inst[14:12]), .b(3'b101), .eq(comparator_31_eq));  // open: gt, lt
  Comparator #(.width(3)) comparator_32 (.a(inst[14:12]), .b(3'b110), .eq(comparator_32_eq));  // open: gt, lt
  Comparator #(.width(3)) comparator_33 (.a(inst[14:12]), .b(3'b111), .eq(comparator_33_eq));  // open: gt, lt
  or or_4 (or_4_out, I2, jal);
  Comparator #(.width(7)) comparator_34 (.a({7{1'b0}}), .b(inst[31:25]), .eq(comparator_34_eq));  // open: gt, lt
  Comparator #(.width(7)) comparator_35 (.a(inst[31:25]), .b(7'b0100000), .eq(comparator_35_eq));  // open: gt, lt
  or or_5 (CSRWen, Icsrw, Icsrwi);
  not not_1 (not_1_out, comparator_23_eq);
  Comparator #(.width(7)) comparator_36 (.a(inst[6:0]), .b(7'b0010011), .eq(I1));  // open: gt, lt
  or or_6 (or_6_out, I2, ILoad);
  Priority_Encoder #(.select(2)) priority_encoder_1 (
    .in0(ILoad), .in1(alu), .in2(or_4_out), .out(WBSel));  // open: in3, gs, en_out, en_in
  Priority_Encoder #(.select(1)) priority_encoder_2 (
    .in0(Icsrw), .in1(Icsrwi), .out(CSRSel));  // open: gs, en_out, en_in
  and and_13 (Radd, R, comparator_22_eq, comparator_23_eq);
  and and_14 (Rmul, R, comparator_24_eq, comparator_22_eq);
  and and_15 (Rsub, R, comparator_25_eq, comparator_22_eq);
  and and_16 (Rsll, R, comparator_26_eq, comparator_23_eq);
  and and_17 (Rmulh, R, comparator_26_eq, comparator_24_eq);
  and and_18 (Rmulhu, R, comparator_27_eq);
  and and_19 (Rslt, R, comparator_28_eq);
  and and_20 (Rxor, R, comparator_29_eq);
  and and_21 (Rsrl, R, comparator_23_eq, comparator_30_eq);
  and and_22 (Rsra, R, not_1_out, comparator_31_eq);
  and and_23 (R_or, R, comparator_32_eq);
  and and_24 (Rand, R, comparator_33_eq);
  not not_2 (alu, or_6_out);
  and and_25 (Isrli, and_8_out, comparator_34_eq);
  and and_26 (Israi, comparator_35_eq, and_8_out);
  Priority_Encoder #(.select(4)) priority_encoder_3 (
    .in0(Iaddi), .in1(Islli), .in2(Islti), .in3(1'b0), .in4(Ixori), .in5(Isrli), .in6(Iori), .in7(Iandi),
    .in8(1'b0), .in9(1'b0), .in10(1'b0), .in11(1'b0), .in12(1'b0), .in13(Israi), .in14(1'b0), .in15(lui),
    .out(priority_encoder_3_out));  // open: gs, en_out, en_in
  Multiplexer #(.enable("false"), .width(4)) multiplexer_1 (
    .in0(4'b0000), .in1(priority_encoder_3_out), .out(ALUSel_I), .sel(I1));
  assign ALUSel = ALUSel_I | ALUSel_R;  // OR_Gate or_7, 4 bits wide
  Priority_Encoder #(.select(4)) priority_encoder_4 (
    .in0(Radd), .in1(Rsll), .in2(Rslt), .in3(1'b0), .in4(Rxor), .in5(Rsrl), .in6(R_or), .in7(Rand),
    .in8(Rmul), .in9(Rmulh), .in10(1'b0), .in11(Rmulhu), .in12(Rsub), .in13(Rsra), .in14(1'b0), .in15(1'b0),
    .out(priority_encoder_4_out));  // open: gs, en_out, en_in
  or or_8 (BSel, MemRW, jal, I, U, SB);
  Priority_Encoder priority_encoder_5 (
    .in0(1'b0), .in1(I), .in2(MemRW), .in3(SB), .in4(U), .in5(jal), .in6(1'b0), .in7(1'b0), .out(ImmSel));  // open: en_in, gs, en_out
  not not_3 (BrGe, or_9_out);
  or or_9 (or_9_out, BrEq, BrLt);
  not not_4 (not_4_out, BrEq);
  not not_5 (not_5_out, BrLt);
  not not_6 (not_6_out, BrLt);
  and and_27 (and_27_out, BrEq, SBbeq);
  and and_28 (and_28_out, not_4_out, SBbne);
  and and_29 (and_29_out, not_5_out, SBbge);
  and and_30 (and_30_out, BrLt, SBbltu);
  and and_31 (and_31_out, BrLt, SBblt);
  and and_32 (and_32_out, not_6_out, SBbgeu);
  Multiplexer #(.enable("false"), .width(4)) multiplexer_2 (
    .in0(4'b0000), .in1(priority_encoder_4_out), .out(ALUSel_R), .sel(R));
  or or_10 (ASel, SB, jal, auipc);
  or or_11 (or_11_out, and_27_out, and_28_out, and_29_out, and_30_out, and_31_out, and_32_out);
  Comparator #(.width(3)) comparator_37 (.a(inst[14:12]), .b(3'b000), .eq(comparator_37_eq));  // open: gt, lt
  Comparator #(.width(3)) comparator_38 (.a(inst[14:12]), .b(3'b001), .eq(comparator_38_eq));  // open: gt, lt
  Comparator #(.width(3)) comparator_39 (.a(inst[14:12]), .b(3'b100), .eq(comparator_39_eq));  // open: gt, lt
  Comparator #(.width(3)) comparator_40 (.a(inst[14:12]), .b(3'b101), .eq(comparator_40_eq));  // open: gt, lt
  Comparator #(.width(3)) comparator_41 (.a(inst[14:12]), .b(3'b110), .eq(comparator_41_eq));  // open: gt, lt
  Comparator #(.width(3)) comparator_42 (.a(inst[14:12]), .b(3'b111), .eq(comparator_42_eq));  // open: gt, lt
  and and_33 (and_33_out, SB, or_11_out);
  or or_12 (BrUn, SBbltu, SBbgeu);
  or or_13 (RegWEn, R, I, U, jal);
  or or_14 (PCSel, and_33_out, jal, I2);
  Comparator #(.width(7)) comparator_43 (.a(inst[6:0]), .b(7'b1100011), .eq(SB));  // open: gt, lt
  and and_34 (SBbeq, SB, comparator_37_eq);
  and and_35 (SBbne, SB, comparator_38_eq);
  and and_36 (SBblt, SB, comparator_39_eq);
  and and_37 (SBbge, SB, comparator_40_eq);
  and and_38 (SBbltu, SB, comparator_41_eq);
  and and_39 (SBbgeu, SB, comparator_42_eq);
  Comparator #(.width(7)) comparator_44 (.a(inst[6:0]), .b(7'b0010111), .eq(auipc));  // open: gt, lt
  Comparator #(.width(7)) comparator_45 (.a(inst[6:0]), .b(7'b0110111), .eq(lui));  // open: gt, lt
  Comparator #(.width(7)) comparator_46 (.a(inst[6:0]), .b(7'b1101111), .eq(jal));  // open: gt, lt
  or or_15 (U, auipc, lui);

  // Other names for the same wires on the sheet: Ijalr = I2; opcode[6:0] = inst[6:0]; rd[4:0] = inst[11:7];
  //   func3[2:0] = inst[14:12]; rs1[4:0] = inst[19:15]; rs2[4:0] = inst[24:20]; func7[6:0] = inst[31:25]; UJ = jal;
  //   S = MemRW

  // Notes on the sheet:
  //   INPUTS to your circuit
  //   DON'T CHANGE THE LOCATIONS OF THE INPUTS AND OUTPUTS!
  //   OUTPUT from your circuit
endmodule
