// Logisim project cpu.circ as structural Verilog: 1 circuit, main circuit cpu
module cpu (
  input  clk,
  input  [31:0] INSTRUCTION,
  input  [31:0] READ_DATA,
  output [31:0] WRITE_ADDRESS,
  output [31:0] PROGRAM_COUNTER,
  output [31:0] ra,
  output [31:0] sp,
  output [31:0] t0,
  output [31:0] t1,
  output [31:0] t2,
  output [31:0] s0,
  output [31:0] s1,
  output [31:0] a0,
  output [31:0] tohost,
  output [3:0] WRITE_ENABLE,
  output [31:0] WRITE_DATA
);

  wire ASel, branch_comp_1_breq, branch_comp_1_brlt, control_logic_1_brun, control_logic_1_bsel,
       control_logic_1_csrsel, control_logic_1_csrwen, control_logic_1_regwen, lb, lh, lw, PCSel, S, sb, sh,
       sw;
  wire [1:0] control_logic_1_wbsel, WRITE_Sel;
  wire [2:0] control_logic_1_immsel, func3;
  wire [3:0] ALUSel, wen_sb, wen_sh;
  wire [4:0] multiplexer_3_out, rd, rs1;
  wire [6:0] register_1_q;
  wire [7:0] multiplexer_9_out;
  wire [11:0] csr_add;
  wire [15:0] multiplexer_10_out;
  wire [31:0] and_1_out, bit_extender_1_out, BYTE_DATA, HALF_DATA, IMM, LOAD_DATA, multiplexer_1_out,
       multiplexer_2_out, multiplexer_5_out, multiplexer_6_out, multiplexer_7_out, multiplexer_8_out,
       PC_add4, regfile_1_read_data_1, register_2_q, WRITE_DATA0;

  assign and_1_out = 32'hfffffffe & WRITE_ADDRESS;  // AND_Gate and_1, 32 bits wide
  Register #(.width(32)) register_1 (
    .D(multiplexer_2_out), .clk(clk), .Q({csr_add, rs1, func3, rd, register_1_q}));  // open: en, clr
  Multiplexer #(.enable("false"), .width(32)) multiplexer_1 (
    .in0(PC_add4), .in1(and_1_out), .out(multiplexer_1_out), .sel(PCSel));
  Adder #(.width(32)) adder_1 (.a(PROGRAM_COUNTER), .b(32'h4), .out(PC_add4));  // open: cin, cout
  Register #(.width(32)) PC (.D(multiplexer_1_out), .clk(clk), .Q(PROGRAM_COUNTER));  // open: en, clr
  Multiplexer #(.enable("false"), .width(32)) multiplexer_2 (
    .in0(INSTRUCTION), .in1(32'h13), .out(multiplexer_2_out), .sel(PCSel));
  Comparator #(.width(3)) comparator_1 (.a(func3), .b(3'b000), .eq(lb));  // open: gt, lt
  Comparator #(.width(3)) comparator_2 (.a(func3), .b(3'b001), .eq(lh));  // open: gt, lt
  Comparator #(.width(3)) comparator_3 (.a(func3), .b(3'b010), .eq(lw));  // open: gt, lt
  Priority_Encoder #(.select(2)) priority_encoder_1 (
    .in0(1'b1), .in1(sb), .in2(sh), .in3(sw), .out(WRITE_Sel));  // open: gs, en_out, en_in
  Register #(.width(32)) register_2 (.D(PROGRAM_COUNTER), .clk(clk), .Q(register_2_q));  // open: en, clr
  control_logic control_logic_1 (
    .CSRWen(control_logic_1_csrwen), .PCSel(PCSel), .RegWEn(control_logic_1_regwen),
    .ImmSel(control_logic_1_immsel), .BrUn(control_logic_1_brun), .ASel(ASel), .BSel(control_logic_1_bsel),
    .ALUSel(ALUSel), .MemRW(S), .WBSel(control_logic_1_wbsel), .CSRSel(control_logic_1_csrsel),
    .inst({csr_add, rs1, func3, rd, register_1_q}), .BrEq(branch_comp_1_breq), .BrLt(branch_comp_1_brlt));
  and and_2 (sb, S, lb);
  and and_3 (sh, S, lh);
  and and_4 (sw, S, lw);
  imm_gen imm_gen_1 (.inst({csr_add, rs1, func3, rd, register_1_q}), .ImmSel(control_logic_1_immsel), .imm(IMM));
  Shifter #(.width(4)) shifter_1 (.in(4'b0001), .\dist (WRITE_ADDRESS[1:0]), .out(wen_sb));
  Shifter #(.width(4)) shifter_2 (.in(4'b0011), .\dist (WRITE_ADDRESS[1:0]), .out(wen_sh));
  regfile regfile_1 (
    .rs1(rs1), .rs2(csr_add[4:0]), .rd(rd), .Write_Data(multiplexer_8_out), .RegWEn(control_logic_1_regwen),
    .clk(clk), .ra(ra), .sp(sp), .t0(t0), .t1(t1), .t2(t2), .s0(s0), .s1(s1), .a0(a0),
    .Read_Data_1(regfile_1_read_data_1), .Read_Data_2(WRITE_DATA0));
  branch_comp branch_comp_1 (
    .rs1(regfile_1_read_data_1), .rs2(WRITE_DATA), .BrUn(control_logic_1_brun), .BrEq(branch_comp_1_breq),
    .BrLt(branch_comp_1_brlt));
  assign bit_extender_1_out = {{27{rs1[4]}}, rs1};  // Bit_Extender bit_extender_1
  Shifter #(.width(32)) shifter_3 (.in(WRITE_DATA0), .\dist (multiplexer_3_out), .out(WRITE_DATA));
  Multiplexer #(.enable("false"), .select(2), .width(5)) multiplexer_3 (
    .in0({5{1'b0}}), .in1(5'b01000), .in2(5'b10000), .in3(5'b11000), .out(multiplexer_3_out),
    .sel(WRITE_ADDRESS[1:0]));
  Multiplexer #(.enable("false"), .select(2), .width(4)) multiplexer_4 (
    .in1(wen_sb), .in2(wen_sh), .in3(4'b1111), .out(WRITE_ENABLE), .sel(WRITE_Sel));  // open: in0
  Multiplexer #(.enable("false"), .width(32)) multiplexer_5 (
    .in0(regfile_1_read_data_1), .in1(bit_extender_1_out), .out(multiplexer_5_out),
    .sel(control_logic_1_csrsel));
  Multiplexer #(.enable("false"), .width(32)) multiplexer_6 (
    .in0(regfile_1_read_data_1), .in1(register_2_q), .out(multiplexer_6_out), .sel(ASel));
  Multiplexer #(.enable("false"), .width(32)) multiplexer_7 (
    .in0(WRITE_DATA0), .in1(IMM), .out(multiplexer_7_out), .sel(control_logic_1_bsel));
  alu alu_1 (.Result(WRITE_ADDRESS), .A(multiplexer_6_out), .B(multiplexer_7_out), .ALUSel(ALUSel));
  // csr csr_1: pin names not known; wires that end beside it: csr_add, multiplexer_5_out, control_logic_1_csrwen, clk, tohost
  Multiplexer #(.enable("false"), .select(2), .width(32)) multiplexer_8 (
    .in0(LOAD_DATA), .in1(WRITE_ADDRESS), .in2(PROGRAM_COUNTER), .out(multiplexer_8_out),
    .sel(control_logic_1_wbsel));  // open: in3
  Multiplexer #(.enable("false"), .select(2), .width(8)) multiplexer_9 (
    .in0(READ_DATA[7:0]), .in1(READ_DATA[15:8]), .in2(READ_DATA[23:16]), .in3(READ_DATA[31:24]),
    .out(multiplexer_9_out), .sel(WRITE_ADDRESS[1:0]));
  Multiplexer #(.enable("false"), .select(2), .width(16)) multiplexer_10 (
    .in0(READ_DATA[15:0]), .in1(READ_DATA[23:8]), .in2(READ_DATA[31:16]), .out(multiplexer_10_out),
    .sel(WRITE_ADDRESS[1:0]));  // open: in3
  assign BYTE_DATA = {{24{multiplexer_9_out[7]}}, multiplexer_9_out};  // Bit_Extender bit_extender_2
  assign HALF_DATA = {{16{multiplexer_10_out[15]}}, multiplexer_10_out};  // Bit_Extender bit_extender_3
  Multiplexer #(.enable("false"), .select(3), .width(32)) multiplexer_11 (
    .in0(BYTE_DATA), .in1(HALF_DATA), .in2(READ_DATA), .in3({32{1'b0}}), .in4({32{1'b0}}), .in5({32{1'b0}}),
    .in6({32{1'b0}}), .in7({32{1'b0}}), .out(LOAD_DATA), .sel(func3));

  // Other names for the same wires on the sheet: rs2[4:0] = csr_add[4:0]; WORD_DATA[31:0] = READ_DATA;
  //   mem_pos[1:0] = WRITE_ADDRESS[1:0]

  // Notes on the sheet:
  //   Output to IMEM
  //   IMEM (do **NOT** move this)
  //   Inputs from IMEM
  //   Inputs/Outputs for testing. Do **NOT** move these.
  //   Outputs To DMEM
  //   DMEM (do **NOT** move this)
  //   Inputs From DMEM
endmodule
