// Logisim project regfile.circ as structural Verilog: 1 circuit, main circuit regfile
module regfile (
  input  [4:0] rs1,
  input  [4:0] rs2,
  input  [4:0] rd,
  input  [31:0] Write_Data,
  input  RegWEn,
  input  clk,
  output [31:0] ra,
  output [31:0] sp,
  output [31:0] t0,
  output [31:0] t1,
  output [31:0] t2,
  output [31:0] s0,
  output [31:0] s1,
  output [31:0] a0,
  output [31:0] Read_Data_1,
  output [31:0] Read_Data_2
);

  wire w0, w1, w2, w3, w4, w5, w6, w7, w8, w9, w10, w11, w12, w13, w14, w15, w16, w17, w18, w19, w20, w21,
       w22, w23, w24, w25, w26, w27, w28, w29, w30, w31;
  wire [31:0] a1, a2, a3, a4, a5, a6, a7, gp, s2, s3, s4, s5, s6, s7, s8, s9, s10, s11, t3, t4, t5, t6, tp,
       x0;

  Demultiplexer #(.enable("false"), .select(5)) demultiplexer_1 (
    .out0(w0), .out1(w1), .out2(w2), .out3(w3), .out4(w4), .out5(w5), .out6(w6), .out7(w7), .out8(w8),
    .out9(w9), .out10(w10), .out11(w11), .out12(w12), .out13(w13), .out14(w14), .out15(w15), .out16(w16),
    .out17(w17), .out18(w18), .out19(w19), .out20(w20), .out21(w21), .out22(w22), .out23(w23), .out24(w28),
    .out25(w25), .out26(w26), .out27(w27), .out28(w28), .out29(w29), .out30(w30), .out31(w31), .in(RegWEn),
    .sel(rd));
  Register #(.width(32)) u_x0 (.D({32{1'b0}}), .en(w0), .clk(clk), .Q(x0));  // open: clr
  Register #(.width(32)) x8 (.D(Write_Data), .en(w8), .clk(clk), .Q(s0));  // open: clr
  Register #(.width(32)) x16 (.D(Write_Data), .en(w16), .clk(clk), .Q(a6));  // open: clr
  Register #(.width(32)) x24 (.D(Write_Data), .en(w24), .clk(clk), .Q(s8));  // open: clr
  Register #(.width(32)) x1 (.D(Write_Data), .en(w1), .clk(clk), .Q(ra));  // open: clr
  Register #(.width(32)) x9 (.D(Write_Data), .en(w9), .clk(clk), .Q(s1));  // open: clr
  Register #(.width(32)) x17 (.D(Write_Data), .en(w17), .clk(clk), .Q(a7));  // open: clr
  Register #(.width(32)) x25 (.D(Write_Data), .en(w25), .clk(clk), .Q(s9));  // open: clr
  Register #(.width(32)) x2 (.D(Write_Data), .en(w2), .clk(clk), .Q(sp));  // open: clr
  Register #(.width(32)) x10 (.D(Write_Data), .en(w10), .clk(clk), .Q(a0));  // open: clr
  Register #(.width(32)) x18 (.D(Write_Data), .en(w18), .clk(clk), .Q(s2));  // open: clr
  Register #(.width(32)) x26 (.D(Write_Data), .en(w26), .clk(clk), .Q(s10));  // open: clr
  Register #(.width(32)) x3 (.D(Write_Data), .en(w3), .clk(clk), .Q(gp));  // open: clr
  Register #(.width(32)) x11 (.D(Write_Data), .en(w11), .clk(clk), .Q(a1));  // open: clr
  Register #(.width(32)) x19 (.D(Write_Data), .en(w19), .clk(clk), .Q(s3));  // open: clr
  Register #(.width(32)) x27 (.D(Write_Data), .en(w27), .clk(clk), .Q(s11));  // open: clr
  Register #(.width(32)) x4 (.D(Write_Data), .en(w4), .clk(clk), .Q(tp));  // open: clr
  Register #(.width(32)) x12 (.D(Write_Data), .en(w12), .clk(clk), .Q(a2));  // open: clr
  Register #(.width(32)) x20 (.D(Write_Data), .en(w20), .clk(clk), .Q(s4));  // open: clr
  Register #(.width(32)) x28 (.D(Write_Data), .en(w28), .clk(clk), .Q(t3));  // open: clr
  Register #(.width(32)) x5 (.D(Write_Data), .en(w5), .clk(clk), .Q(t0));  // open: clr
  Register #(.width(32)) x13 (.D(Write_Data), .en(w13), .clk(clk), .Q(a3));  // open: clr
  Register #(.width(32)) x21 (.D(Write_Data), .en(w21), .clk(clk), .Q(s5));  // open: clr
  Register #(.width(32)) x29 (.D(Write_Data), .en(w29), .Q(t4));  // open: clk, clr
  Register #(.width(32)) x6 (.D(Write_Data), .en(w6), .clk(clk), .Q(t1));  // open: clr
  Register #(.width(32)) x14 (.D(Write_Data), .en(w14), .Q(a4));  // open: clk, clr
  Register #(.width(32)) x22 (.D(Write_Data), .en(w22), .clk(clk), .Q(s6));  // open: clr
  Register #(.width(32)) x30 (.D(Write_Data), .en(w30), .clk(clk), .Q(t5));  // open: clr
  Register #(.width(32)) x7 (.D(Write_Data), .en(w7), .clk(clk), .Q(t2));  // open: clr
  Register #(.width(32)) x15 (.D(Write_Data), .en(w15), .clk(clk), .Q(a5));  // open: clr
  Register #(.width(32)) x23 (.D(Write_Data), .en(w23), .clk(clk), .Q(s7));  // open: clr
  Register #(.width(32)) x31 (.D(Write_Data), .en(w31), .clk(clk), .Q(t6));  // open: clr
  Multiplexer #(.enable("false"), .select(5), .width(32)) multiplexer_1 (
    .in0(x0), .in1(ra), .in2(sp), .in3(gp), .in4(tp), .in5(t0), .in6(t1), .in7(t2), .in8(s0), .in9(s1),
    .in10(a0), .in11(a1), .in12(a2), .in13(a3), .in14(a4), .in15(a5), .in16(a6), .in17(a7), .in18(s2),
    .in19(s3), .in20(s4), .in21(s5), .in22(s6), .in23(s7), .in24(s8), .in25(s9), .in26(s10), .in27(s11),
    .in28(t3), .in29(t4), .in30(t5), .in31(t6), .out(Read_Data_1), .sel(rs1));
  Multiplexer #(.enable("false"), .select(5), .width(32)) multiplexer_2 (
    .in0(x0), .in1(ra), .in2(sp), .in3(gp), .in4(tp), .in5(t0), .in6(t1), .in7(t2), .in8(s0), .in9(s1),
    .in10(a0), .in11(a1), .in12(a2), .in13(a3), .in14(a4), .in15(a5), .in16(a6), .in17(a7), .in18(s2),
    .in19(s3), .in20(s4), .in21(s5), .in22(s6), .in23(s7), .in24(s8), .in25(s9), .in26(s10), .in27(s11),
    .in28(t3), .in29(t4), .in30(t5), .in31(t6), .out(Read_Data_2), .sel(rs2));

  // Other names for the same wires on the sheet: read_data1[31:0] = Read_Data_1; read_data2[31:0] = Read_Data_2;
  //   read_reg1[4:0] = rs1; read_reg2[4:0] = rs2; write_en = RegWEn; write_reg[4:0] = rd

  // Notes on the sheet:
  //   INPUTS to your circuit
  //   DON'T CHANGE THE LOCATIONS OF THE INPUTS AND OUTPUTS!
  //   These are DEBUG/TEST outputs from your circuit.
  //   OUTPUTS from your circuit
endmodule
