// Logisim project cpu-memory2.circ as structural Verilog: 1 circuit, main circuit run_main
module run_main (
  output [31:0] ra,
  output [31:0] sp,
  output [31:0] t0,
  output [31:0] t1,
  output [31:0] t2,
  output [31:0] s0,
  output [31:0] s1,
  output [31:0] a0,
  output [31:0] Requested_Address,
  output [31:0] Requested_Instruction,
  output [15:0] Time_Step,
  output halt
);

  wire clk;

  Clock clock_1 (.out(clk));
  // Probe on Requested_Address
  cpu_harness cpu_harness_1 (
    .INSTRUCTION(Requested_Instruction), .clk(clk), .PROGRAM_COUNTER(Requested_Address), .ra(ra), .sp(sp),
    .t0(t0), .t1(t1), .t2(t2), .s0(s0), .s1(s1), .a0(a0));
  ROM #(.addrWidth(14), .dataWidth(32)) rom_1 (.addr(Requested_Address[15:2]), .data(Requested_Instruction));
  // Probe on Requested_Instruction
  Counter #(.max('hffff), .width(16)) counter_1 (.clk(clk), .Q(Time_Step));  // open: clr, load, up, count, D, carry
  Comparator #(.width(16)) comparator_1 (.a(Time_Step), .b(16'h69), .eq(halt));  // open: gt, lt

  // Other names for the same wires on the sheet: INSTRUCTION[31:0] = Requested_Instruction;
  //   PROGRAM_COUNTER[31:0] = Requested_Address

  // Notes on the sheet:
  //   contents of rom_1 (hex, n*v repeats v):
  //   FF00C93 100293 10433 F000D13 19D00A3 5C8CB3 19D0023 5C8CB3 19D00A3 5C8CB3 19D0123 5C8CB3 19D01A3
  //   5C8CB3 19D0223 D0903 1D0983 2D0903 3D0983 4D0983 64C8C93 5C8CB3 19D0223 4D1A03 5C8CB3 19D0423 8D1A03
  //   11800D13 8C9C13 5C8CB3 19D1023 D1B83 11800D13 FF00313 5C8CB3 19D2423 5C8CB3 19D2623 5C8CB3 19D2823
  //   8D2303 CD2383 10D2E03 19C6BB3 10B9B13 17B6AB3 4D2403 6D1483 7D0903 8D0983 1248533 FF600293 3E800313
  //   F17 128293 2D663 F0067 14A0533 14A0533
  //   Instruction Memory
  //   Halts Execution After Constant # of Clock Cycles
  //   Constant
endmodule
