// Logisim project cpu-sbtype.circ as structural Verilog: 1 circuit, main circuit run_main
module run_main (
  output [31:0] ra,
  output [31:0] sp,
  output [31:0] t0,
  output [31:0] t1,
  output [31:0] t2,
  output [31:0] s0,
  output [31:0] s1,
  output [31:0] a0,
  output [31:0] Requested_Address,
  output [31:0] Requested_Instruction,
  output [15:0] Time_Step,
  output halt
);

  wire clk;

  Clock clock_1 (.out(clk));
  // Probe on Requested_Address
  cpu_harness cpu_harness_1 (
    .INSTRUCTION(Requested_Instruction), .clk(clk), .PROGRAM_COUNTER(Requested_Address), .ra(ra), .sp(sp),
    .t0(t0), .t1(t1), .t2(t2), .s0(s0), .s1(s1), .a0(a0));
  ROM #(.addrWidth(14), .dataWidth(32)) rom_1 (.addr(Requested_Address[15:2]), .data(Requested_Instruction));
  // Probe on Requested_Instruction
  Counter #(.max('hffff), .width(16)) counter_1 (.clk(clk), .Q(Time_Step));  // open: clr, load, up, count, D, carry
  Comparator #(.width(16)) comparator_1 (.a(Time_Step), .b(16'h63), .eq(halt));  // open: gt, lt

  // Other names for the same wires on the sheet: INSTRUCTION[31:0] = Requested_Instruction;
  //   PROGRAM_COUNTER[31:0] = Requested_Address

  // Notes on the sheet:
  //   contents of rom_1 (hex, n*v repeats v):
  //   B7 FFFFF137 208C63 110A63 2210033 402000B3 401000B3 208863 217133 2101B3 210863 FFFFF137 8133
  //   FE2086E3 B7 FFFFF137 2001B3 311A63 211863 2210033 401000B3 209A63 217133 2101B3 FFF18193 211863
  //   FFFFF137 8133 FE2014E3 B7 FFFFF137 2001B3 314E63 214C63 2210033 401000B3 10B7 114C63 20CA63 217133
  //   2101B3 FFF18213 324863 FFFFF137 8133 FE2044E3 20B7 FFFFF137 20DE63 100213 225A63 2210033 401000B3
  //   10B7 215A63 217133 2101B3 FFF18213 41D863 FFFFF137 11B7 FE3154E3 B7 FFFFF137 2001B3 316E63 216C63
  //   2210033 401000B3 10B7 116C63 20EA63 217133 2101B3 FFF18213 326863 FFFFF137 8133 FE2064E3 20B7
  //   FFFFF137 20FE63 100213 227A63 2210033 401000B3 10B7 217A63 217133 2101B3 FFF18213 41F863 FFFFF137
  //   11B7 FE3174E3
  //   Instruction Memory
  //   Halts Execution After Constant # of Clock Cycles
  //   Constant
endmodule
